// Logisim project GuessTheNumber.circ as structural Verilog: 9 circuits, main circuit main
module main (
  input  in_1,
  input  in_2,
  input  in_3,
  input  in_4,
  input  in_5,
  input  in_6,
  input  in_7,
  input  in_8
);
endmodule

module game (
  input  Jogar,
  input  A,
  input  B,
  input  Jogador,
  output maior,
  output out_6,
  output igual,
  output menor
);

  mux mux_1 (.A(A), .B(B), .S(Jogador), .C(out_6));
  comparador comparador ();  // open: A0, A1, A2, A3, B0, B1, B2, B3, Maior, Igual, Menor
  // AND_Gate and_1 is placed but not wired
  // AND_Gate and_2 is placed but not wired
  // AND_Gate and_3 is placed but not wired
endmodule

module mux (
  input  A,
  input  B,
  input  S,
  output C
);

  wire and_1_out, and_2_out, not_1_out;

  not not_1 (not_1_out, S);
  and and_1 (and_1_out, not_1_out, A);
  and and_2 (and_2_out, S, B);
  or or_1 (C, and_1_out, and_2_out);
endmodule

// comp
module comparador (
  input  A0,
  input  A1,
  input  A2,
  input  A3,
  input  B0,
  input  B1,
  input  B2,
  input  B3,
  output Maior,
  output Igual,
  output Menor
);

  maiorque_4_bits maiorque_4_bits_1 (
    .A0(A0), .B0(B0), .A1(A1), .B1(B1), .A2(A2), .B2(B2), .A3(A3), .B3(B3), .out_9(Maior));
  igualdade_4_bits igualdade_4_bits_1 (
    .A0(A0), .B0(B0), .A1(A1), .B1(B1), .A2(A2), .B2(B2), .A3(A3), .B3(B3), .out_9(Igual));
  maiorque_4_bits maiorque_4_bits_2 (
    .A0(B0), .B0(A0), .A1(B1), .B1(A1), .A2(B2), .B2(A2), .A3(B3), .B3(A3), .out_9(Menor));

  // Notes on the sheet:
  //   Maior
  //   Menor
endmodule

module mux2x1_4_bits (
  input  S,
  input  A0,
  input  B0,
  input  A1,
  input  B1,
  input  A2,
  input  B2,
  input  A3,
  input  B3,
  output C0,
  output C1,
  output C2,
  output C3
);

  mux mux_1 (.A(A0), .B(B0), .S(S), .C(C0));
  mux mux_2 (.A(A1), .B(B1), .S(S), .C(C1));
  mux mux_3 (.A(A2), .B(B2), .S(S), .C(C2));
  mux mux_4 (.A(A3), .B(B3), .S(S), .C(C3));
endmodule

// igual
module igualdade (
  input  A,
  input  B,
  output S
);

  wire and_1_out, and_2_out, not_1_out, not_2_out;

  not not_1 (not_1_out, A);
  and and_1 (and_1_out, not_1_out, not_2_out);
  not not_2 (not_2_out, B);
  and and_2 (and_2_out, A, B);
  or or_1 (S, and_1_out, and_2_out);
endmodule

// igual
module igualdade_4_bits (
  input  A0,
  input  B0,
  input  A1,
  input  B1,
  input  A2,
  input  B2,
  input  A3,
  input  B3,
  output out_9
);

  wire igualdade_1_s, igualdade_2_s, igualdade_3_s, igualdade_4_s;

  igualdade igualdade_1 (.A(A0), .B(B0), .S(igualdade_1_s));
  igualdade igualdade_2 (.A(A1), .B(B1), .S(igualdade_2_s));
  igualdade igualdade_3 (.A(A2), .B(B2), .S(igualdade_3_s));
  igualdade igualdade_4 (.A(A3), .B(B3), .S(igualdade_4_s));
  and and_1 (out_9, igualdade_1_s, igualdade_2_s, igualdade_3_s, igualdade_4_s);
endmodule

// maior/menor
module maiorque_4_bits (
  input  A0,
  input  B0,
  input  A1,
  input  B1,
  input  A2,
  input  B2,
  input  A3,
  input  B3,
  output out_9
);

  wire and_1_out, and_2_out, and_3_out, igualdade_1_s, igualdade_2_s, igualdade_3_s, maiorque_1_s,
       maiorque_2_s, maiorque_3_s, maiorque_4_s;

  maiorque maiorque_1 (.A(A0), .B(B0), .S(maiorque_1_s));
  igualdade igualdade_1 (.A(A1), .B(B1), .S(igualdade_1_s));
  maiorque maiorque_2 (.A(A1), .B(B1), .S(maiorque_2_s));
  igualdade igualdade_2 (.A(A2), .B(B2), .S(igualdade_2_s));
  maiorque maiorque_3 (.A(A2), .B(B2), .S(maiorque_3_s));
  igualdade igualdade_3 (.A(A3), .B(B3), .S(igualdade_3_s));
  and and_1 (and_1_out, maiorque_1_s, igualdade_1_s, igualdade_2_s, igualdade_3_s);
  and and_2 (and_2_out, maiorque_2_s, igualdade_2_s, igualdade_3_s);
  and and_3 (and_3_out, maiorque_3_s, igualdade_3_s);
  maiorque maiorque_4 (.A(A3), .B(B3), .S(maiorque_4_s));
  or or_1 (out_9, and_1_out, and_2_out, and_3_out, maiorque_4_s);
endmodule

// maior
module maiorque (
  input  A,
  input  B,
  output S
);

  wire not_1_out;

  not not_1 (not_1_out, B);
  and and_1 (S, A, not_1_out);
endmodule
